# Fritzing sketch Marshall Bot with Correct wiring (saved by Fritzing 0.9.9b)
circuit board: 10cm x 6cm
breadboards: 1

parts:
  Part2 = Arduino Uno (Rev3) - ICSP
  J9 = Basic Servo
  J10 = Infrared Proximity Sensor
  J11 = Infrared Proximity Sensor
  J12 = Infrared Proximity Sensor
  J13 = Basic Servo
  J14 = Basic Servo
  J15 = Basic Servo
  C2 = Electrolytic Capacitor [capacitance=100μF voltage=35V package="0807 [SMD, electrolytic]"]
  LCD3 = LCD screen
  LCM1602_IIC3 = LCM1602 IIC [part_number="LCM1602 IIC" chip_label="LCM1602 IIC" package="DIP (Dual Inline) [THT]"]
  NRF24L1 = NRF24L01

nets:
  N1: Part2.A0, J12.Vout
  N2: Part2.A1, J11.Vout
  N3: Part2.A2, J10.Vout
  N4: Part2.A4/SDA, LCM1602_IIC3.SDA
  N5: Part2.A5/SCL, LCM1602_IIC3.SCL
  N6: Part2.D8, NRF24L1.CSN
  N7: Part2.D11_PWM/MOSI, NRF24L1.MOSI
  N8: Part2.D12/MISO, NRF24L1.MISO
  N9: Part2.D13/SCK, NRF24L1.SCK
  GND: Part2.GND, J9.gnd, J10.GND, J11.GND, J12.GND, J13.gnd, J14.gnd, J15.gnd, C2.-, LCM1602_IIC3.GND, NRF24L1.GND
  N10: Part2.D2, J13.pulse
  N11: Part2.D3_PWM, J9.pulse
  N12: Part2.D4, J15.pulse
  N13: Part2.D5_PWM, J14.pulse
  N14: Part2.D7, NRF24L1.CE
  3V3: Part2.3V3, NRF24L1.VCC
  VCC: Part2.5V, J10.Vcc, J11.Vcc, J12.Vcc, C2.+, LCM1602_IIC3.VCC
  VCC_2: J9.vcc, J13.vcc, J14.vcc, J15.vcc
  N15: LCD3.RS, LCM1602_IIC3.RS
  N16: LCD3.R/W, LCM1602_IIC3.RW
  N17: LCD3.E, LCM1602_IIC3.E
  N18: LCD3.DB0, LCM1602_IIC3.D0
  N19: LCD3.DB1, LCM1602_IIC3.D1
  N20: LCD3.DB2, LCM1602_IIC3.D2
  N21: LCD3.DB3, LCM1602_IIC3.D3
  N22: LCD3.DB4, LCM1602_IIC3.D4
  N23: LCD3.DB5, LCM1602_IIC3.D5
  N24: LCD3.DB6, LCM1602_IIC3.D6
  N25: LCD3.DB7, LCM1602_IIC3.D7
  N26: LCD3.LED+, LCM1602_IIC3.A
  N27: LCD3.LED-, LCM1602_IIC3.K
  N28: LCM1602_IIC3.LED_A, LCM1602_IIC3.LED_B

notes:
  IR 3 (Right)
  IR 2 (Center)
  IR 1 (Left)
  Servo 1 (Left)
  Servo 2 (Left top)
  Servo 3 (Right)
  Servo 4 (Right top)

custom parts:
  LCM1602 IIC: I2C-Module to use a 1602 or 2004 LCD on with the wire.h libory Serial LCD Modul
  NRF24L01: NRF24L01 module
